// Logisim project HC_circuit_21100602.circ as structural Verilog: 7 circuits, main circuit main
module main (
  input  in_1,
  input  in_2,
  input  in_3,
  input  in_4
);

  wire _0_out, _1_out, _2_out, _3_out, _4_out, _5_out, _6_out, _7_out, _8_out, _9_out, _10_out, _11_out,
       _12_out, _13_out, _14_out, _15_out, priority_encoder_1_en_out, priority_encoder_1_gs,
       priority_encoder_2_en_out, priority_encoder_2_gs, priority_encoder_3_en_out, priority_encoder_3_gs,
       priority_encoder_4_en_out, priority_encoder_4_gs;
  wire [0:0] not_1_out;
  wire [1:0] generator_1_r0, priority_encoder_1_out, priority_encoder_5_out;
  wire [2:0] checker_1_out_10, not_3_out;
  wire [3:0] corrector_1_out_8;

  Button _0 (.out(_0_out));
  Button _1 (.out(_1_out));
  Button _2 (.out(_2_out));
  Button _3 (.out(_3_out));
  Button _4 (.out(_4_out));
  Button _5 (.out(_5_out));
  Button _6 (.out(_6_out));
  Button _7 (.out(_7_out));
  Button _8 (.out(_8_out));
  Button _9 (.out(_9_out));
  Button _10 (.out(_10_out));
  Button _11 (.out(_11_out));
  Button _12 (.out(_12_out));
  Button _13 (.out(_13_out));
  Button _14 (.out(_14_out));
  Button _15 (.out(_15_out));
  Priority_Encoder #(.select(2)) priority_encoder_1 (
    .in0(_0_out), .in1(_1_out), .in2(_2_out), .in3(_3_out), .out(priority_encoder_1_out),
    .gs(priority_encoder_1_gs), .en_out(priority_encoder_1_en_out), .en_in(priority_encoder_2_en_out));
  Priority_Encoder #(.select(2)) priority_encoder_2 (
    .in0(_4_out), .in1(_5_out), .in2(_6_out), .in3(_7_out), .out(priority_encoder_1_out),
    .gs(priority_encoder_2_gs), .en_out(priority_encoder_2_en_out), .en_in(priority_encoder_3_en_out));
  Priority_Encoder #(.select(2)) priority_encoder_3 (
    .in0(_8_out), .in1(_9_out), .in2(_10_out), .in3(_11_out), .out(priority_encoder_1_out),
    .gs(priority_encoder_3_gs), .en_out(priority_encoder_3_en_out), .en_in(priority_encoder_4_en_out));
  Priority_Encoder #(.select(2)) priority_encoder_4 (
    .in0(_12_out), .in1(_13_out), .in2(_14_out), .in3(_15_out), .out(priority_encoder_1_out),
    .gs(priority_encoder_4_gs), .en_out(priority_encoder_4_en_out));  // open: en_in
  Priority_Encoder #(.select(2)) priority_encoder_5 (
    .in0(priority_encoder_1_gs), .in1(priority_encoder_2_gs), .in2(priority_encoder_3_gs),
    .in3(priority_encoder_4_gs), .out(priority_encoder_5_out));  // open: gs, en_out, en_in
  not not_1 (not_1_out[0], priority_encoder_1_out[0]);
  Hex_Digit_Display hex_digit_display_1 (.value({priority_encoder_5_out, priority_encoder_1_out[1], not_1_out[0]}));  // open: dp
  Hex_Digit_Display hex_digit_display_2 (.value({priority_encoder_5_out, priority_encoder_1_out}));  // open: dp
  Checker checker_1 (
    .a3(priority_encoder_5_out[1]), .a2(priority_encoder_5_out[0]), .a1(priority_encoder_1_out[1]),
    .a0(not_1_out[0]), .r2(not_3_out[2]), .r1(not_3_out[1]), .r0(not_3_out[0]), .out_8(checker_1_out_10[2]),
    .out_9(checker_1_out_10[1]), .out_10(checker_1_out_10[0]));
  Generator generator_1 (
    .a3(priority_encoder_5_out[1]), .a2(priority_encoder_5_out[0]), .a1(priority_encoder_1_out[1]),
    .a0(priority_encoder_1_out[0]), .r2(not_3_out[2]), .r1(generator_1_r0[1]), .r0(generator_1_r0[0]));
  Hex_Digit_Display hex_digit_display_3 (.value({in_1, checker_1_out_10}));  // open: dp
  Hex_Digit_Display hex_digit_display_4 (.value({in_3, not_3_out}));  // open: dp
  not not_2 (not_3_out[1], generator_1_r0[1]);
  not not_3 (not_3_out[0], generator_1_r0[0]);
  Hex_Digit_Display hex_digit_display_5 (.value({in_4, not_3_out[2], generator_1_r0}));  // open: dp
  corrector corrector_1 (
    .a0(not_1_out[0]), .a1(priority_encoder_1_out[1]), .a2(priority_encoder_5_out[0]),
    .a3(priority_encoder_5_out[1]), .out_8(corrector_1_out_8[0]), .out_9(corrector_1_out_8[1]),
    .out_10(corrector_1_out_8[2]), .out_11(corrector_1_out_8[3]), .s2(checker_1_out_10[2]),
    .s1(checker_1_out_10[1]), .s0(checker_1_out_10[0]));
  Hex_Digit_Display hex_digit_display_6 (.value(corrector_1_out_8));  // open: dp

  // Notes on the sheet:
  //   b3b2b1b0
  //   a3
  //   a2
  //   a3a2a1a0
  //   a1
  //   a0
  //   r1
  //   r0
  //   r2
  //   r2r1r0
endmodule

module Generator (
  input  a3,
  input  a2,
  input  a1,
  input  a0,
  output r2,
  output r1,
  output r0
);

  Adder adder_1 (.in_1(a3), .in_2(a2), .in_3(a0), .out_4(r2));
  Adder adder_2 (.in_1(a3), .in_2(a1), .in_3(a0), .out_4(r1));
  Adder adder_3 (.in_1(a2), .in_2(a1), .in_3(a0), .out_4(r0));
endmodule

module Adder (
  input  in_1,
  input  in_2,
  input  in_3,
  output out_4
);

  wire and_1_out, and_2_out, not_1_out, not_2_out, xor_1_out;

  not not_1 (not_1_out, in_1);
  xor xor_1 (xor_1_out, in_2, in_3);
  not not_2 (not_2_out, xor_1_out);
  and and_1 (and_1_out, not_1_out, xor_1_out);
  and and_2 (and_2_out, in_1, not_2_out);
  or or_1 (out_4, and_2_out, and_1_out);
endmodule

module Checker (
  input  a3,
  input  a2,
  input  a1,
  input  a0,
  input  r2,
  input  r1,
  input  r0,
  output out_8,
  output out_9,
  output out_10
);

  get_4bit_piroty get_4bit_piroty_1 (.in_1(a3), .in_2(a2), .in_3(a0), .in_4(r2), .out_5(out_8));
  get_4bit_piroty get_4bit_piroty_2 (.in_1(a3), .in_2(a1), .in_3(a0), .in_4(r1), .out_5(out_9));
  get_4bit_piroty get_4bit_piroty_3 (.in_1(a2), .in_2(a1), .in_3(a0), .in_4(r0), .out_5(out_10));
endmodule

module get_4bit_piroty (
  input  in_1,
  input  in_2,
  input  in_3,
  input  in_4,
  output out_5
);

  wire xor_1_out, xor_2_out;

  xor xor_1 (xor_1_out, in_1, in_2);
  xor xor_2 (xor_2_out, in_3, in_4);
  xor xor_3 (out_5, xor_1_out, xor_2_out);
endmodule

module corrector (
  input  a0,
  input  a1,
  input  a2,
  input  a3,
  input  s2,
  input  s1,
  input  s0,
  output out_8,
  output out_9,
  output out_10,
  output out_11
);

  wire and_1_out, and_2_out, and_3_out, and_4_out, not_1_out, not_2_out, not_3_out;

  not not_1 (not_1_out, s2);
  not not_2 (not_2_out, s1);
  Conditional_not_gate conditional_not_gate_1 (.To_be_invert(a1), .condition(and_1_out), .out_3(out_9));
  and and_1 (and_1_out, not_1_out, s1, s0);
  not not_3 (not_3_out, s0);
  Conditional_not_gate conditional_not_gate_2 (.To_be_invert(a2), .condition(and_2_out), .out_3(out_10));
  and and_2 (and_2_out, not_2_out, s2, s0);
  Conditional_not_gate conditional_not_gate_3 (.To_be_invert(a3), .condition(and_3_out), .out_3(out_11));
  and and_3 (and_3_out, not_3_out, s2, s1);
  and and_4 (and_4_out, s2, s1, s0);
  Conditional_not_gate conditional_not_gate_4 (.To_be_invert(a0), .condition(and_4_out), .out_3(out_8));
endmodule

module Conditional_not_gate (
  input  To_be_invert,
  input  condition,
  output out_3
);

  wire and_1_out, and_2_out, not_1_out, not_2_out;

  not not_1 (not_1_out, condition);
  not not_2 (not_2_out, To_be_invert);
  and and_1 (and_1_out, To_be_invert, not_1_out);
  and and_2 (and_2_out, not_2_out, condition);
  or or_1 (out_3, and_1_out, and_2_out);
endmodule
